# Fritzing sketch KnockLock (saved by Fritzing 0.9.3b)
breadboards: 2

parts:
  Part3 = Arduino Uno (Rev3)
  J3 = Piezo Speaker
  S2 = Pushbutton [package="[THT]"]
  R6 = Resistor [tolerance=±5% resistance=10k package=THT]
  LED3 = LED - 5mm [color="Green (560nm)" package="5 mm [THT]"]
  LED4 = LED - 5mm [color="Red (633nm)" package="5 mm [THT]"]
  R7 = Resistor [tolerance=±5% resistance=560 package=THT]
  R8 = Resistor [tolerance=±5% resistance=560 package=THT]
  R10 = Resistor [tolerance=±5% resistance=1M package=THT]
  S3 = Taiway 100-SP-X-T1 SPDT Miniature Toggle Switch [part_number=100-SP-X-T1-0-0-B1-M1 package=THT]  # not connected
  Part4 = Arduino Uno (Rev3)
  LCD2 = LCD screen [part_number="HELLO WORLD !!!"]
  R11 = Resistor [tolerance=±5% resistance=220 package="2512 [SMD]"]
  J5 = Basic Servo

nets:
  N1: Part3.A0, J3.pin2, R10.Pin_1
  N2: Part3.D9_PWM, J5.pulse
  N3: Part3.GND, J3.pin1, R10.Pin_0
  N4: Part3.D2, S2.Pin_3, S2.Pin_4, R6.Pin_0
  N5: Part3.D4, R8.Pin_1
  N6: Part3.D5_PWM, R7.Pin_1
  N7: S2.Pin_1, S2.Pin_2, J5.vcc
  N8: R6.Pin_1, LED3.cathode, LED4.cathode, J5.gnd
  N9: LED3.anode, R7.Pin_0
  N10: LED4.anode, R8.Pin_0
  N11: Part4.D11_PWM/MOSI, LCD2.R/W, LCD2.E, LCD2.DB0, LCD2.DB1
  N12: Part4.D12/MISO, LCD2.RS
  N13: Part4.D2, LCD2.DB7
  N14: Part4.D3_PWM, LCD2.DB6
  N15: Part4.D4, LCD2.DB5
  N16: Part4.D5_PWM, LCD2.DB4
  VSS: LCD2.VSS, LCD2.VDD, LCD2.LED-, R11.Pin_0
  N17: LCD2.LED+, R11.Pin_1

notes:
  10kΩ
